# Fritzing sketch Arduino_Nano_RDM6300_oled (saved by Fritzing 0.9.3b)

parts:
  Часть1 = Arduino Nano (Rev3.0)
  RDM1 = RDM6300
  Grove1 = Grove OLED 128x96

nets:
  GND: Часть1.GND, RDM1.GND, Grove1.GND
  N1: Часть1.D10, RDM1.Tx
  5V: Часть1.5V, RDM1.5V
  N2: Часть1.A5, Grove1.SCL
  N3: Часть1.A4, Grove1.SDA
  3V3: Часть1.3V3, Grove1.VCC

notes:
  to antenna
